# Fritzing sketch orphybot_controller_v2 (saved by Fritzing 0.8.7b)
breadboards: 1

parts:
  Part2 = Arduino Nano (Rev3.0)
  Part3 = Thumb Joystick
  Part4 = Thumb Joystick
  Transceiver1 = nRF24L01 [package=module]
  VCC1 = Battery
  AMS1 = AMS1777 5V regulator module

nets:
  GND: Part2.GND, Part3.GND, Part4.GND, Transceiver1.GND, AMS1.GND-_(output)
  N1: Part2.D2, Part3.SEL
  N2: Part2.D3, Part4.SEL
  N3: Part2.D9, Transceiver1.CSN
  N4: Part2.D10, Transceiver1.CE
  N5: Part2.D11/MOSI, Transceiver1.MOSI
  N6: Part2.D12/MISO, Transceiver1.MISO
  VCC: Part2.VIN, Part3.VCC, Part4.VCC, Transceiver1.VCC, AMS1.VOUT+
  N7: Part2.A4, Part4.HORZ
  N8: Part2.A3, Part4.VERT
  N9: Part2.A1, Part3.HORZ
  N10: Part2.A0, Part3.VERT
  N11: Part2.D13/SCK, Transceiver1.SCK
  N12: VCC1.-, AMS1.GND-_(input)
  N13: VCC1.+, AMS1.VIN+

custom parts:
  nRF24L01: nRF24L01 module
  Battery: Your standard 2x 18650 battery pack (7,4 Volts)
  AMS1777 5V regulator module: AMS1777 5V regulator module source : https://github.com/ShenTengTu/fritzing_parts/tree/master/voltage%20regulator/AMS1117_5V_regulator_module
