# Fritzing sketch orphybot_testbed_-_wiring_v2 (saved by Fritzing 0.9.3b)
breadboards: 1

parts:
  Part1 = Arduino Uno (Rev3) - ICSP
  L298N1 = L298N DC motor driver
  L298N2 = L298N DC motor driver
  M1 = DC Motor
  M2 = DC Motor
  M4 = DC Motor
  M5 = DC Motor
  HC-1 = HC-12 Module
  Part2 = Arduino Nano (Rev3.0)
  HC-SR04_Sensor_1 = HC-SR04 Ultrasonic Distance Sensor
  S14 = SWITCH-DPDT [package=eg2211]
  VCC1 = Battery
  M6 = RioRand LM2596
  J8 = Screw terminal - 2 pins [package=THT]
  J10 = Screw terminal - 2 pins [package=THT]
  J11 = Screw terminal - 2 pins [package=THT]
  J13 = Screw terminal - 2 pins [package=THT]
  J14 = Screw terminal - 2 pins [package=THT]
  J15 = Screw terminal - 2 pins [package=THT]
  Antenna1 = HC-12 Antenna
  Part3 = Voltage Sensor 25V
  Part4 = ACS712 Low Current Sensor Board v12

nets:
  N1: Part1.A4/SDA, Part2.A4, Part2.A3
  N2: Part1.A5/SCL, Part2.A5
  N3: Part1.ICSP_MISO, Part1.D12/MISO, L298N2.5V#10, L298N2.IN4
  N4: Part1.ICSP_MOSI, Part1.D11_PWM/MOSI, L298N2.ENB
  N5: Part1.D8, L298N2.IN1
  N6: Part1.D9_PWM, L298N2.ENA
  N7: Part1.D10_PWM/SS, L298N1.ENB
  N8: Part1.D13/SCK, L298N2.IN3
  N9: Part1.D0/RX, HC-1.SET, HC-1.TXD
  N10: Part1.D1/TX, HC-1.RXD
  N11: Part1.D2, L298N1.IN1
  N12: Part1.D3_PWM, L298N1.ENA
  N13: Part1.D4, L298N1.IN2
  N14: Part1.D5_PWM, L298N1.IN3
  N15: Part1.D6_PWM, L298N1.IN4
  N16: Part1.D7, L298N2.IN2
  GND: Part1.GND, L298N1.GND, HC-1.GND, J15.pin2
  VCC: Part1.VIN, L298N1.12V, L298N1.5V, L298N2.12V, L298N2.5V#7, HC-1.VCC, Part2.VIN, HC-SR04_Sensor_1.VCC, S14.4, M6.Pin_1, M6.Pin_3, J8.pin1, J8.pin2, J10.pin1, J10.pin2, J11.pin1, J11.pin2, J13.pin1, J13.pin2, Part3.VCC, Part3.+, Part4.VO
  N17: L298N1.OUT1, M5.pin_2
  N18: L298N1.OUT2, M5.pin_1
  N19: L298N1.OUT3, M4.pin_2
  N20: L298N1.OUT4, M4.pin_1
  N21: L298N2.OUT1, M1.pin_2
  N22: L298N2.OUT2, M1.pin_1
  N23: L298N2.OUT3, M2.pin_2
  N24: L298N2.OUT4, M2.pin_1
  N25: L298N2.GND, J15.pin1
  N26: HC-1.ANT, Antenna1.ANT
  GND_2: Part2.GND, Part2.RESET, J14.pin2, Part3.-, Part4.GND
  N27: Part2.D8, HC-SR04_Sensor_1.TRIG
  N28: Part2.D9, Part2.D10, HC-SR04_Sensor_1.ECHO
  N29: Part2.A1, Part4.5V
  N30: Part2.A0, Part3.S
  N31: HC-SR04_Sensor_1.GND, J14.pin1
  N32: S14.2, Part4.IP+
  N33: S14.1, M6.Pin_2, M6.Pin_4, Part3.GND
  N34: S14.5, VCC1.+
  N35: VCC1.-, Part4.IP-

custom parts:
  L298N DC motor driver: 2x DC motor driver with 78M05 positive voltage regulator (7..35 V) L298N: max 46 V, 2 A Set 5 V Enable jumper to enable 5 V regultor (needed for the L298N) and +5 V output at screw terminal or supply external +5 V at screw terminal Set ENA and/or ENB to +5 V to enable motor permanently or supply ENA and/or ENB with PWM signal IN1 and IN2 set rotation directory for motor A (OUT1/OUT2) IN2 and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
  HC-12 Module: HC-12 433Mhz Module
  Battery: Your standard 2x 18650 battery pack (7,4 Volts)
  HC-12 Antenna: Antenna for HC-12 433Mhz Module
