# Fritzing sketch orphybot_testbed_controller (saved by Fritzing 0.9.3b)
breadboards: 1

parts:
  Part1 = Arduino Nano (Rev3.0)
  HC-1 = HC-12 Module
  Antenna1 = HC-12 Antenna
  Part2 = Thumb Joystick
  LED1 = LEDs [package=led10mm]
  LED2 = LEDs [package=led10mm]
  LED3 = LEDs [package=led10mm]
  R1 = Resistor [tolerance=±5% resistance=220 package="0805 [SMD]"]
  R2 = Resistor [tolerance=±5% resistance=220 package="0805 [SMD]"]
  R3 = Resistor [tolerance=±5% resistance=220 package="0805 [SMD]"]

nets:
  N1: Part1.D1/TX, HC-1.RXD
  N2: Part1.D0/RX, HC-1.TXD
  GND: Part1.GND, HC-1.GND, Part2.GND, LED1.C, LED2.C, LED3.C
  VCC: Part1.5V, HC-1.VCC, Part2.VCC, R1.Pin_0, R2.Pin_0, R3.Pin_0
  N3: Part1.A1, Part2.VERT
  N4: Part1.A0, Part2.HORZ
  N5: HC-1.ANT, Antenna1.ANT
  N6: LED1.A, R2.Pin_1
  N7: LED2.A, R3.Pin_1
  N8: LED3.A, R1.Pin_1

custom parts:
  HC-12 Module: HC-12 433Mhz Module
  HC-12 Antenna: Antenna for HC-12 433Mhz Module
